# Fritzing sketch FSR (saved by Fritzing 0.7.4b)
breadboards: 1

parts:
  Arduino1 = Arduino
  R1 = Basic Force Sensing Resistor (FSR) [part_number=A201 package=THT]
  R2 = Resistor [tolerance=±5% resistance=10k package=THT]

nets:
  N1: Arduino1.GND, R2.Pin_1
  N2: Arduino1.+5V, R1.pin_0
  N3: Arduino1.A0, R1.pin_1, R2.Pin_0
